# Fritzing sketch Arduino-PWM-Fan-Control (saved by Fritzing 1.0.6)
perfboards: 1

parts:
  Part2 = Arduino Nano (Rev3.0) (ICSP)
  F1 = Fan - 4 wire [package=THT]

nets:
  N1: Part2.D3, F1.Tach
  N2: Part2.D5, F1.PWM

custom parts:
  Fan - 4 wire: Fan, 4 wire with tach.
